# Fritzing sketch ESP32+LORA+GPS+OLED (saved by Fritzing 0.9.4)

parts:
  MH-ET_Live_Minikit_for_ESP1 = MH-ET Live Minikit for ESP32
  GY-NEO6MV3 = SUP500F [package=sup500f]
  LoRa_Module1 = Ra-01 - LoRa Module SX1278 [part_number=SX1278]
  part = single row smd female pin header, 1 pin [form="♀ (female)" part_number=reset]
  part_2 = single row smd female pin header, 1 pin [form="♀ (female)" part_number=DIO0]
  part_3 = single row smd female pin header, 1 pin [form="♀ (female)" part_number="LORA CLK"]
  part_4 = single row smd female pin header, 1 pin [form="♀ (female)" part_number=MISO]
  part_5 = female pin header, 2 pins [form="♀ (female)" part_number="TX RX"]
  part_6 = single row smd male pin header, 1 pin [form="♂ (male)" part_number=MOSI]
  part_7 = female pin header, 1 pin [form="♀ (female)" part_number="LORA NSS"]
  S1 = Pushbutton [package="[SMD]"]
  OLED1 = OLED 128x64 I2C Monochrome Display

nets:
  N1: MH-ET_Live_Minikit_for_ESP1.IO34, GY-NEO6MV3.TX-O, part_5.pin2
  N2: MH-ET_Live_Minikit_for_ESP1.TMS, S1.Pin_3, S1.Pin_4
  N3: MH-ET_Live_Minikit_for_ESP1.IO26, LoRa_Module1.DIO0, part_2.pin1
  N4: MH-ET_Live_Minikit_for_ESP1.IO18, LoRa_Module1.NSS, part_7.pin1
  N5: MH-ET_Live_Minikit_for_ESP1.IO19, LoRa_Module1.MOSI, part_4.pin1
  N6: MH-ET_Live_Minikit_for_ESP1.IO23, LoRa_Module1.RESET, part.pin1
  N7: MH-ET_Live_Minikit_for_ESP1.IO5, LoRa_Module1.SCK, part_3.pin1
  3.3V: MH-ET_Live_Minikit_for_ESP1.3.3V, GY-NEO6MV3.VCC, LoRa_Module1.3.3V, OLED1.VDD
  N8: MH-ET_Live_Minikit_for_ESP1.IO22, OLED1.SCK
  N9: MH-ET_Live_Minikit_for_ESP1.IO21, OLED1.SDA
  GND: MH-ET_Live_Minikit_for_ESP1.GND, GY-NEO6MV3.RX-I, LoRa_Module1.GND, S1.Pin_1, S1.Pin_2, OLED1.GND
  N10: MH-ET_Live_Minikit_for_ESP1.IO27, LoRa_Module1.MISO, part_6.pin1
  N11: MH-ET_Live_Minikit_for_ESP1.TDI, GY-NEO6MV3.GND, part_5.pin1

notes:
  SX1276 PIN ESP32
  CLK 18 5
  MISO 19 19
  MOSI 23 27
  CS 5 18
  RST 14(TMS) 23
  DIO0 26 26
  NEO6M wire color ESP32
  TX yellow 34 RX
  RX orange 12 TX
  Service Button
  GPIO14 on D1 Mini
  GPIO38 on TBEAM
  128 x 64 OLED SSD1306
  OLED wire color ESP32
  SDA purple 21
  SCL blue 22

custom parts:
  MH-ET Live Minikit for ESP32: MH-ET Live Minikit for ESP32 ( http://mh.nodebb.com/topic/8/mh-et-live-minikit-for-esp32/2/) PCB footprint is invalid.
  Ra-01 - LoRa Module SX1278: The Ra-01 LoRa Module featuring the SX1278 engine by Semtech. Module by AI-Thinker. Module (Ra-01) specifications from: https://www.banggood.com/Ra-01-Smart-Electronics-SX1278-LoRa-Spread-Spectrum-Wireless-Module-Ultra-Far-10KM-433M-p-1130769.html Description: Power supply: DC1.8-3.7V(3.3V) Chip: SX1278 Frequency: 433Mhz Operating temperature: -40~+85°C On Sheild Description (may vary by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
